# Fritzing sketch buzzer1 (saved by Fritzing 0.9.2b)
circuit board: 6.88566cm x 5.36311cm

parts:
  J1 = Piezo Speaker
  Arduino1 = Arduino Uno (Rev3)

nets:
  N1: J1.pin1, Arduino1.GND
  N2: J1.pin2, Arduino1.D9_PWM

notes:
  Piezoelectric speakers are frequently used as beepers in watches and other electronic devices. In this project, a piezo speaker is used to play melodies. It sends a square wave of the appropriate frequency to the piezo, generating the corresponding tone.
  http://arduino.cc/en/Tutorial/Melody

// code stored in the sketch: Melody.ino
int speakerPin = 9;

int length = 15; // the number of notes
char notes[] = "ccggaagffeeddc "; // a space represents a rest
int beats[] = { 1, 1, 1, 1, 1, 1, 2, 1, 1, 1, 1, 1, 1, 2, 4 };
int tempo = 300;

void playTone(int tone, int duration) {
  for (long i = 0; i < duration * 1000L; i += tone * 2) {
    digitalWrite(speakerPin, HIGH);
    delayMicroseconds(tone);
    digitalWrite(speakerPin, LOW);
    delayMicroseconds(tone);
  }
}

void playNote(char note, int duration) {
  char names[] = { 'c', 'd', 'e', 'f', 'g', 'a', 'b', 'C' };
  int tones[] = { 1915, 1700, 1519, 1432, 1275, 1136, 1014, 956 };

  // play the tone corresponding to the note name
  for (int i = 0; i < 8; i++) {
    if (names[i] == note) {
      playTone(tones[i], duration);
    }
  }
}

void setup() {
  pinMode(speakerPin, OUTPUT);
}

void loop() {
  for (int i = 0; i < length; i++) {
    if (notes[i] == ' ') {
      delay(beats[i] * tempo); // rest
    } else {
      playNote(notes[i], beats[i] * tempo);
    }

    // pause between notes
    delay(tempo / 2); 
  }
}
